# Fritzing sketch connect-esp8266v1-software (saved by Fritzing 0.9.3b)

parts:
  Part1 = Arduino Uno (Rev3)
  U1 = ESP8266 WiFi Module [part_number=ESP8266]
  R2 = Resistor [tolerance=±5% resistance=1k package=THT]
  R3 = Resistor [tolerance=±5% resistance=1k package=THT]
  R4 = Resistor [tolerance=±5% resistance=1k package=THT]

nets:
  RX: Part1.D12/MISO, R2.Pin_0, R3.Pin_1
  TX: Part1.D13/SCK, U1.RXD
  GND: Part1.GND, U1.GND, R4.Pin_0
  3.3V: Part1.3V3, U1.VCC, U1.CH_PD
  N1: U1.TXD, R2.Pin_1
  N2: R3.Pin_0, R4.Pin_1

notes:
  ESP8266 V1 Tutorial, Ket noi module ESP8266 V1 voi Arduino Uno, 1.4

custom parts:
  ESP8266 WiFi Module: Generic WiFi Module based on the ESP8266 with onboard PCB antenna and UART communications
