# Fritzing sketch upload-firmware-esp8266v1 (saved by Fritzing 0.9.3b)

parts:
  Part1 = Arduino Uno (Rev3)
  U1 = ESP8266 WiFi Module [part_number=ESP8266]
  R1 = Resistor [tolerance=±5% resistance=1k package=THT]
  R2 = Resistor [tolerance=±5% resistance=1k package=THT]
  R3 = Resistor [tolerance=±5% resistance=1k package=THT]
  R4 = Resistor [tolerance=±5% resistance=1k package=THT]

nets:
  GND: Part1.GND, Part1.RESET, U1.GPIO_0, U1.GND, R4.Pin_0
  RX: Part1.D0/RX, U1.RXD
  TX: Part1.D1/TX, R2.Pin_0, R3.Pin_1
  3.3V: Part1.3V3, U1.VCC, R1.Pin_0
  N1: U1.CH_PD, R1.Pin_1
  N2: U1.TXD, R2.Pin_1
  N3: R3.Pin_0, R4.Pin_1

notes:
  ESP8266 V1 Tutorial, Su dung Arduino Uno upload firmware cho module ESP8266 V1, 1.0

custom parts:
  ESP8266 WiFi Module: Generic WiFi Module based on the ESP8266 with onboard PCB antenna and UART communications
